// Logisim project cpu.circ as structural Verilog: 1 circuit, main circuit cpu
module cpu (
  input  clk,
  input  [31:0] INSTRUCTION,
  input  [31:0] READ_DATA,
  output [31:0] WRITE_ADDRESS,
  output [31:0] PROGRAM_COUNTER,
  output [31:0] ra,
  output [31:0] sp,
  output [31:0] t0,
  output [31:0] t1,
  output [31:0] t2,
  output [31:0] s0,
  output [31:0] s1,
  output [31:0] a0,
  output [31:0] tohost,
  output [3:0] WRITE_ENABLE,
  output [31:0] WRITE_DATA
);

  wire alu_1_p1, alu_1_p6, alu_1_p7, alu_1_p9, ASel, BrEq, BrLt, BrUn, BSel, CSR_WE, CSRSel, PCSel,
       regfile_1_p7, regfile_1_p8, regfile_1_p10, regfile_1_p22, regfile_1_p24, regfile_1_p26, RegWEn;
  wire [1:0] WBSel;
  wire [2:0] control_logic_1_immsel;
  wire [3:0] ALUOp;
  wire [11:0] bit_extender_2_out;
  wire [31:0] adder_1_out, bit_extender_1_out, imm, multiplexer_1_out, multiplexer_2_out, multiplexer_3_out,
       multiplexer_4_out, multiplexer_5_out, regfile_1_p20, regfile_1_p21;

  Adder #(.width(32)) adder_1 (.a(PROGRAM_COUNTER), .b(32'h4), .out(adder_1_out));  // open: cin, cout
  Multiplexer #(.enable("false"), .width(32)) multiplexer_1 (
    .in0(adder_1_out), .in1(WRITE_ADDRESS), .out(multiplexer_1_out), .sel(PCSel));
  Register #(.width(32)) PC (.D(multiplexer_1_out), .clk(clk), .Q(PROGRAM_COUNTER));  // open: en, clr
  control_logic control_logic_1 (
    .CSRWen(CSR_WE), .PCSel(PCSel), .RegWEn(RegWEn), .ImmSel(control_logic_1_immsel), .BrUn(BrUn),
    .ASel(ASel), .BSel(BSel), .ALUSel(ALUOp), .WBSel(WBSel), .CSRSel(CSRSel), .inst(INSTRUCTION),
    .BrEq(BrEq), .BrLt(BrLt));  // open: MemRW
  imm_gen imm_gen_1 (.inst(INSTRUCTION), .ImmSel(control_logic_1_immsel), .imm(imm));
  Multiplexer #(.enable("false"), .select(2), .width(32)) multiplexer_2 (
    .in0(WRITE_ADDRESS), .out(multiplexer_2_out), .sel(2'b00));  // open: in1, in2, in3
  // regfile regfile_1: pin names not known; wires that end beside it: INSTRUCTION[19:15], INSTRUCTION[24:20], INSTRUCTION[11:7], multiplexer_2_out, RegWEn, clk, regfile_1_p7, regfile_1_p8, regfile_1_p8, regfile_1_p10, regfile_1_p10, ra, sp, t0, t1, t2, s0, s1, a0, regfile_1_p20, regfile_1_p21, regfile_1_p22, regfile_1_p22, regfile_1_p24, regfile_1_p24, regfile_1_p26, regfile_1_p26
  branch_comp branch_comp_1 (.rs1(regfile_1_p20), .rs2(regfile_1_p21), .BrUn(BrUn), .BrEq(BrEq), .BrLt(BrLt));
  assign bit_extender_1_out = {{27{INSTRUCTION[19]}}, INSTRUCTION[19:15]};  // Bit_Extender bit_extender_1
  Bit_Extender #(.in_width(32), .out_width(12)) bit_extender_2 (.in(imm), .out(bit_extender_2_out));
  Multiplexer #(.enable("false"), .width(32)) multiplexer_3 (
    .in0(regfile_1_p20), .in1(bit_extender_1_out), .out(multiplexer_3_out), .sel(CSRSel));
  Multiplexer #(.enable("false"), .width(32)) multiplexer_4 (
    .in0(regfile_1_p20), .in1(PROGRAM_COUNTER), .out(multiplexer_4_out), .sel(ASel));
  Multiplexer #(.enable("false"), .width(32)) multiplexer_5 (
    .in0(imm), .in1(regfile_1_p21), .out(multiplexer_5_out), .sel(BSel));
  // csr csr_1: pin names not known; wires that end beside it: bit_extender_2_out, multiplexer_3_out, CSR_WE, clk, tohost
  // alu alu_1: pin names not known; wires that end beside it: alu_1_p1, multiplexer_4_out, multiplexer_5_out, ALUOp, WRITE_ADDRESS, alu_1_p6, alu_1_p7, alu_1_p7, alu_1_p9

  assign WRITE_ENABLE = 4'b0000;

  // Other names for the same wires on the sheet: ALURes[31:0] = WRITE_ADDRESS

  // Notes on the sheet:
  //   Output to IMEM
  //   IMEM (do **NOT** move this)
  //   Inputs from IMEM
  //   Inputs/Outputs for testing. Do **NOT** move these.
  //   Outputs To DMEM
  //   DMEM (do **NOT** move this)
  //   Inputs From DMEM
endmodule
